# Fritzing sketch 4 Transistor hearing aid (saved by Fritzing 0.8.7b)
breadboards: 1

parts:
  R1 = Resistor [tolerance=±5% resistance=10k package=THT]
  R2 = Resistor [tolerance=±5% resistance=1M package=THT]
  R3 = Resistor [tolerance=±5% resistance=4.7k package=THT]
  R4 = Resistor [tolerance=±5% resistance=100k package=THT]
  R5 = Resistor [tolerance=±5% resistance=3.9k package=THT]
  R6 = Resistor [tolerance=±5% resistance=1.5k package=THT]
  R7 = Resistor [tolerance=±5% resistance=100k package=THT]
  R8 = Resistor [tolerance=±5% resistance=100 package=THT]
  R9 = Resistor [tolerance=±5% resistance=10k package=THT]
  C1 = Ceramic Capacitor [capacitance=100nF package="100 mil [THT, multilayer]"]
  C2 = Ceramic Capacitor [capacitance=100nF package="100 mil [THT, multilayer]"]
  C3 = Electrolytic Capacitor [capacitance=1µF package="100 mil [THT, electrolytic]"]
  C4 = Electrolytic Capacitor [capacitance=10µF package="100 mil [THT, electrolytic]"]
  C5 = Electrolytic Capacitor [capacitance=470µF package="100 mil [THT, electrolytic]"]
  C6 = Electrolytic Capacitor [capacitance=1µF package="100 mil [THT, electrolytic]"]
  C7 = Ceramic Capacitor [capacitance=470pF package="100 mil [THT, multilayer]"]
  R10 = TRIMPOT [part_number=50K package=trim_pot_pth]
  Q1 = TRANSISTOR_NPN [part_number=BC547 package=to-92-ammo]
  Q2 = TRANSISTOR_NPN [part_number=BC547 package=to-92-ammo]
  Q3 = TRANSISTOR_NPN [part_number=BC547 package=to-92-ammo]
  Q4 = TRANSISTOR_NPN [part_number=BC337 package=to-92-ammo]
  D1 = Rectifier Diode [part_number=1N4148 package="300 mil [THT]"]
  MIC1 = Microphone
  TRS1 = Audio Jack (TRS) 3.5mm [package="4Ucon 08780 [THT]"]
  BAT1 = Battery Holders [package=battery-aa-kit]

nets:
  N1: R1.Pin_0, C1.1, MIC1.pin1
  N2: R1.Pin_1, R3.Pin_1, R5.Pin_1, R7.Pin_1, R8.Pin_0, C5.+
  N3: R2.Pin_0, R6.Pin_1, R7.Pin_0, C4.+
  N4: R2.Pin_1, C1.0, Q1.B
  N5: R3.Pin_0, C2.1, Q1.C
  N6: R4.Pin_0, C2.0, Q2.B
  N7: R4.Pin_1, R5.Pin_0, C3.+, Q2.C
  N8: R6.Pin_0, Q3.C
  N9: R8.Pin_1, TRS1.Ring, BAT1.+
  N10: R9.Pin_0, C6.-, C7.1, Q4.B
  N11: R9.Pin_1, C7.0, Q4.C, TRS1.Tip
  N12: C3.-, R10.CCW, Q3.B, D1.cathode
  N13: C4.-, C5.-, R10.CW, Q1.E, Q2.E, Q3.E, Q4.E, D1.anode, MIC1.pin2, BAT1.-
  N14: C6.+, R10.WIPER
