# Fritzing sketch Hearing aid TDA2822M_2 (saved by Fritzing 0.8.7b)
breadboards: 1

parts:
  R1 = Resistor [tolerance=±5% resistance=2.2k package=THT]
  R2 = Resistor [tolerance=±5% resistance=680 package=THT]
  R3 = Resistor [tolerance=±5% resistance=330k package=THT]
  MIC1 = Microphone
  C1 = Ceramic Capacitor [capacitance=10nF package="100 mil [THT, multilayer]"]
  C2 = Ceramic Capacitor [capacitance=100nF package="100 mil [THT, multilayer]"]
  C4 = Electrolytic Capacitor [capacitance=10µF package="100 mil [THT, electrolytic]"]
  C5 = Ceramic Capacitor [capacitance=0.01µF package="100 mil [THT, multilayer]"]
  R4 = Resistor [tolerance=±5% resistance=4.7 package=THT]
  C6 = Ceramic Capacitor [capacitance=0.1µF package="100 mil [THT, multilayer]"]
  C7 = Ceramic Capacitor [capacitance=0.1µF package="100 mil [THT, multilayer]"]
  R5 = Resistor [tolerance=±5% resistance=4.7 package=THT]
  TRS1 = Audio Jack (TRS) 3.5mm [package="4Ucon 08780 [THT]"]
  BAT1 = Battery Holders [package=battery-aa-panel]
  U3 = TDA2822M [package="DIP8 [THT]"]
  R6 = Trimmer Potentiometer [maximum_resistance=10kΩ package=THT]
  Q1 = NPN-Transistor [part_number=BC547 package="TO92 [THT]"]
  C8 = Electrolytic Capacitor [capacitance=47µF package="100 mil [THT, electrolytic]"]
  C9 = Electrolytic Capacitor [capacitance=100µF package="100 mil [THT, electrolytic]"]
  LED1 = LED - 5mm [color="Red (633nm)" package="5 mm [THT]"]
  R8 = Resistor [tolerance=±5% resistance=220 package=THT]
  R9 = Resistor [tolerance=±5% resistance=100 package=THT]
  R10 = Resistor [tolerance=±5% resistance=33 package=THT]

nets:
  N1: R1.Pin_0, MIC1.pin2, C1.1
  N2: R1.Pin_1, R2.Pin_1, C8.+, R9.Pin_0
  N3: R2.Pin_0, R3.Pin_1, C2.1, Q1.C
  N4: R3.Pin_0, C1.0, Q1.B
  N5: MIC1.pin1, C5.0, R4.Pin_0, R5.Pin_1, BAT1.-, U3.Pin_4, U3.Pin_6, R6.leg2, C8.-, C9.-, LED1.cathode, R10.Pin_0
  N6: C2.0, R6.wiper
  N7: C4.-, C5.1, U3.Pin_5
  N8: C4.+, U3.Pin_8
  N9: R4.Pin_1, C6.0
  N10: C6.1, TRS1.Ring, U3.Pin_3
  N11: C7.0, R5.Pin_0
  N12: C7.1, TRS1.Tip, U3.Pin_1
  N13: BAT1.+, U3.Pin_2, C9.+, R8.Pin_1, R9.Pin_1
  N14: U3.Pin_7, R6.leg1
  N15: Q1.E, R10.Pin_1
  N16: LED1.anode, R8.Pin_0

custom parts:
  TDA2822M: IC AMP AUDIO DUAL LOW VOLT 8MDIP
